// Logisim project Logickokolo.circ as structural Verilog: 1 circuit, main circuit Kolo1
module Kolo1 (
  input  X1,
  input  X2,
  output Y
);

  wire not_1_out, not_2_out, or_1_out, or_2_out;

  // Probe on X1
  not not_1 (not_1_out, X2);
  not not_2 (not_2_out, X1);
  or or_1 (or_1_out, X1, not_1_out);
  or or_2 (or_2_out, not_2_out, X2);
  and and_1 (Y, or_1_out, or_2_out);
  // Probe on Y
endmodule
