// Logisim project ort_domaci2.circ as structural Verilog: 1 circuit, main circuit main
module main (
  input  a,
  input  b,
  input  c,
  input  d,
  input  e,
  output x
);

  wire nor_1_out, nor_2_out, nor_3_out, nor_4_out, nor_5_out, nor_6_out, nor_7_out;

  nor nor_1 (nor_1_out, b, b);
  nor nor_2 (nor_2_out, a, nor_1_out);
  nor nor_3 (nor_3_out, d, e);
  nor nor_4 (nor_4_out, nor_2_out, nor_2_out);
  nor nor_5 (nor_5_out, nor_3_out, nor_3_out);
  nor nor_6 (nor_6_out, nor_4_out, c);
  nor nor_7 (nor_7_out, nor_6_out, nor_6_out);
  nor nor_8 (x, nor_7_out, nor_5_out);

  // Notes on the sheet:
  //   Datum rodjenja 10.07
  //   1+0+0+7=8
endmodule
